// Logisim project GogoS.circ as structural Verilog: 1 circuit, main circuit main
module main (
  output [7:0] out_1,
  output [7:0] out_2,
  output [1:0] Result,
  output [7:0] RegData1,
  output [7:0] Reader,
  output [7:0] out_6,
  output [7:0] RegData2,
  output [7:0] out_8,
  output [7:0] DataMemory,
  output [7:0] out_10,
  output [1:0] out_11
);

  wire and_1_out, and_2_out, and_3_out, and_4_out, and_5_out, and_6_out, and_7_out, clock_1_out,
       decoder_1_out0, decoder_1_out1, decoder_1_out2, decoder_1_out3, MemClock_out, multiplexer_2_out,
       multiplexer_3_out, multiplexer_4_out, multiplexer_5_out, undriven;
  wire [1:0] multiplexer_1_out;
  wire [7:0] adder_1_out, bit_extender_1_out, multiplexer_7_out, multiplexer_9_out, not_1_out, PC_q,
       ram_2_dout, X1_q, X2_q, X3_q, X4_q;

  Clock #(.highDuration(3)) clock_1 (.out(clock_1_out));
  Register PC (.D(adder_1_out), .en(undriven), .clk(clock_1_out), .Q(PC_q));  // open: clr
  RAM #(.enables("line")) ram_1 (
    .addr(PC_q), .we(1'b0), .oe(1'b1), .clk(clock_1_out), .dout({Reader[7:6], out_11, Reader[3:0]}));  // open: din
  assign not_1_out = ~PC_q;  // NOT_Gate not_1, 8 bits wide
  and and_1 (and_1_out, not_1_out[0], not_1_out[1], not_1_out[2], not_1_out[3]);
  and and_2 (and_2_out, not_1_out[4], not_1_out[5], not_1_out[6], not_1_out[7]);
  Adder adder_1 (.a(PC_q), .b(8'h1), .out(adder_1_out));  // open: cin, cout
  and and_3 (and_3_out, and_1_out, and_2_out);
  Adder adder_2 (.a(out_6), .b(bit_extender_1_out), .out(out_8));  // open: cin, cout
  Multiplexer #(.width(2)) multiplexer_1 (.in0(2'b00), .in1(out_11), .out(multiplexer_1_out), .sel(multiplexer_4_out));
  assign bit_extender_1_out = {{6{multiplexer_1_out[1]}}, multiplexer_1_out};  // Bit_Extender bit_extender_1
  Decoder #(.select(2)) decoder_1 (
    .out0(decoder_1_out0), .out1(decoder_1_out1), .out2(decoder_1_out2), .out3(decoder_1_out3),
    .sel(Reader[1:0]), .en(1'b1));
  Multiplexer #(.select(2)) multiplexer_2 (
    .in0(1'b0), .in1(1'b0), .in2(1'b0), .in3(1'b1), .out(multiplexer_2_out), .sel(Reader[7:6]));
  Multiplexer #(.select(2)) multiplexer_3 (
    .in0(1'b0), .in1(1'b0), .in2(1'b0), .in3(1'b1), .out(multiplexer_3_out), .sel(Reader[7:6]));
  Multiplexer #(.select(2)) multiplexer_4 (
    .in0(1'b0), .in1(1'b0), .in2(1'b0), .in3(1'b1), .out(multiplexer_4_out), .sel(Reader[7:6]));
  Multiplexer #(.select(2)) multiplexer_5 (
    .in0(1'b0), .in1(1'b1), .in2(1'b1), .in3(1'b1), .out(multiplexer_5_out), .sel(Reader[7:6]));
  and and_4 (and_4_out, decoder_1_out0, multiplexer_5_out);
  and and_5 (and_5_out, decoder_1_out1, multiplexer_5_out);
  and and_6 (and_6_out, decoder_1_out2, multiplexer_5_out);
  and and_7 (and_7_out, decoder_1_out3, multiplexer_5_out);
  Register X1 (.D(out_10), .en(and_4_out), .clk(clock_1_out), .Q(X1_q), .clr(and_3_out));
  Register X3 (.D(out_10), .en(and_6_out), .clk(clock_1_out), .Q(X3_q), .clr(and_3_out));
  Register X4 (.D(out_10), .en(and_7_out), .clk(clock_1_out), .Q(X4_q), .clr(and_3_out));
  Register X2 (.D(out_10), .en(and_5_out), .clk(clock_1_out), .Q(X2_q), .clr(and_3_out));
  Multiplexer #(.select(2), .width(8)) multiplexer_6 (
    .in0(X1_q), .in1(X2_q), .in2(X3_q), .in3(X4_q), .out(out_6), .sel(Reader[3:2]));
  Multiplexer #(.select(2), .width(8)) multiplexer_7 (
    .in0(X1_q), .in1(X2_q), .in2(X3_q), .in3(X4_q), .out(multiplexer_7_out), .sel(out_11));
  Multiplexer #(.width(8)) multiplexer_8 (
    .in0(multiplexer_7_out), .in1(bit_extender_1_out), .out(RegData2), .sel(multiplexer_4_out));
  Adder adder_3 (.a(out_6), .b(multiplexer_7_out), .out(out_1));  // open: cin, cout
  Hex_Digit_Display hex_digit_display_1 (.value(out_10[7:4]));  // open: dp
  Multiplexer #(.width(8)) multiplexer_9 (.in0(out_1), .in1(out_2), .out(multiplexer_9_out), .sel(multiplexer_2_out));
  Multiplexer #(.width(8)) multiplexer_10 (
    .in0(multiplexer_9_out), .in1(out_8), .out(DataMemory), .sel(multiplexer_3_out));
  Clock MemClock (.out(MemClock_out));
  Hex_Digit_Display hex_digit_display_2 (.value(out_10[3:0]));  // open: dp
  Multiplier multiplier_1 (.a(out_6), .b(multiplexer_7_out), .out(out_2));  // open: cin, cout
  RAM #(.enables("line")) ram_2 (
    .addr(DataMemory), .we(1'b0), .oe(1'b1), .clk(MemClock_out), .dout(ram_2_dout));  // open: din
  Multiplexer #(.width(8)) multiplexer_11 (.in0(DataMemory), .in1(ram_2_dout), .out(out_10), .sel(multiplexer_3_out));

  assign Reader[5:4] = out_11;
  assign RegData1 = out_6;
  assign Result = Reader[1:0];

  // Notes on the sheet:
  //   Binux CPU
  //   IF
  //   Tri Luu
  //   Instruction Memory
  //   PC ADD
  //   I pledge my honor that I have abided by the Stevens Honor System
  //   Immediate
  //   Control signals
  //   ALUsrc
  //   RegWrite
  //   ReadData1
  //   ReadData2
  //   ALU/EX Stage
  //   Arithmetic Add
  //   WB
  //   Arithmetic Mul
  //   ALUout
  //   MemToReg
  //   RegWrite
endmodule
